# Fritzing sketch Diagram (saved by Fritzing 0.9.3b)

parts:
  Relay = Keyes Relay [package=THT]
  WeMos_D1_Mini1 = WeMos D1 Mini
  Relay_2 = Keyes Relay [package=THT]

nets:
  N1: Relay.signal, WeMos_D1_Mini1.D3
  N2: Relay.power, WeMos_D1_Mini1.3V3, Relay_2.power
  N3: Relay.ground, WeMos_D1_Mini1.G, Relay_2.ground
  N4: WeMos_D1_Mini1.D2, Relay_2.signal

notes:
  Garage Door Opener
  ~ AC
  Light Bulb
  5v DC USB Power

custom parts:
  Keyes Relay: The Keyes 5V relay module is suitable for SCM development, home appliance control. It uses a 5V~12V TIL control signal which can control DC / AC signal.
